# Fritzing sketch 8 bulbs LED (saved by Fritzing 0.9.3b)
breadboards: 1

parts:
  LED1 = LED - 5mm [color="Red (633nm)" package="5 mm [THT]"]
  LED2 = LED - 5mm [color="Red (633nm)" package="5 mm [THT]"]
  LED3 = LED - 5mm [color="Red (633nm)" package="5 mm [THT]"]
  LED4 = LED - 5mm [color="Red (633nm)" package="5 mm [THT]"]
  LED5 = LED - 5mm [color="Red (633nm)" package="5 mm [THT]"]
  LED6 = LED - 5mm [color="Red (633nm)" package="5 mm [THT]"]
  LED7 = LED - 5mm [color="Red (633nm)" package="5 mm [THT]"]
  LED8 = LED - 5mm [color="Red (633nm)" package="5 mm [THT]"]
  Part1 = Arduino Uno (Rev3)
  S1 = Pushbutton [package="[THT]"]

nets:
  N1: LED1.cathode, LED2.cathode, LED3.cathode, LED4.cathode, LED5.cathode, LED6.cathode, LED7.cathode, LED8.cathode, Part1.D2, Part1.GND, S1.Pin_1, S1.Pin_2
  N2: LED1.anode, Part1.D13/SCK
  N3: LED2.anode, Part1.D12/MISO
  N4: LED3.anode, Part1.D11_PWM/MOSI
  N5: LED4.anode, Part1.D10_PWM/SS
  N6: LED5.anode, Part1.D9_PWM
  N7: LED6.anode, Part1.D8
  N8: LED7.anode, Part1.D7
  N9: LED8.anode, Part1.D6_PWM
  N10: S1.Pin_3, S1.Pin_4
